// Logisim project Circuitos-M2.circ as structural Verilog: 7 circuits, main circuit main
module main (
  input  [3:0] in_1,
  input  [3:0] in_2,
  input  [6:0] in_3,
  input  [6:0] in_4,
  input  [6:0] in_5,
  input  [6:0] in_6,
  input  [6:0] in_7,
  output [1:0] out_8,
  output [1:0] out_9
);

  wire and_1_out, and_2_out, and_3_out, and_4_out, button_1_out, clock_1_out, clock_2_out,
       controlled_buffer_1_out, controlled_buffer_2_out, controlled_buffer_3_out, controlled_buffer_4_out,
       not_1_out, not_2_out, or_1_out, or_2_out;
  wire [3:0] counter_1_q, counter_2_q;
  wire [15:0] decoder_1_out0, decoder_2_out0, demultiplexer_1_out0, demultiplexer_1_out1,
       demultiplexer_1_out2, demultiplexer_1_out3, demultiplexer_1_out4, demultiplexer_1_out5,
       demultiplexer_1_out6, demultiplexer_1_out7, demultiplexer_1_out8, demultiplexer_1_out9,
       demultiplexer_1_out10, demultiplexer_1_out11, demultiplexer_1_out12, demultiplexer_1_out13,
       demultiplexer_1_out14, demultiplexer_1_out15;

  Joystick_part #(.bits(2)) joystick_1 (.x(out_8), .y(out_9));
  not not_1 (not_1_out, out_8[1]);
  not not_2 (not_2_out, out_9[1]);
  Clock clock_1 (.out(clock_1_out));
  and and_1 (and_1_out, out_8[0], out_8[1]);
  and and_2 (and_2_out, out_8[0], not_1_out);
  Clock clock_2 (.out(clock_2_out));
  and and_3 (and_3_out, out_9[0], out_9[1]);
  and and_4 (and_4_out, out_9[0], not_2_out);
  assign controlled_buffer_1_out = and_1_out ? clock_1_out : 1'bz;  // Controlled_Buffer controlled_buffer_1
  assign controlled_buffer_2_out = or_1_out ? clock_1_out : 1'bz;  // Controlled_Buffer controlled_buffer_2
  or or_1 (or_1_out, and_1_out, and_2_out);
  assign controlled_buffer_3_out = and_4_out ? clock_2_out : 1'bz;  // Controlled_Buffer controlled_buffer_3
  assign controlled_buffer_4_out = or_2_out ? clock_2_out : 1'bz;  // Controlled_Buffer controlled_buffer_4
  or or_2 (or_2_out, and_3_out, and_4_out);
  Counter #(.width(4), .max('hf), .ongoal("stay")) counter_1 (
    .load(controlled_buffer_1_out), .D(counter_1_q), .count(controlled_buffer_2_out), .Q(counter_1_q),
    .clk(controlled_buffer_2_out), .clr(button_1_out));  // open: carry
  Counter #(.width(4), .max('hf), .ongoal("stay")) counter_2 (
    .load(controlled_buffer_3_out), .D(counter_2_q), .count(controlled_buffer_4_out), .Q(counter_2_q),
    .clk(controlled_buffer_4_out), .clr(button_1_out));  // open: carry
  Button button_1 (.out(button_1_out));
  Decoder #(.select(4)) decoder_1 (
    .out0(decoder_1_out0[0]), .out1(decoder_1_out0[1]), .out2(decoder_1_out0[2]), .out3(decoder_1_out0[3]),
    .out4(decoder_1_out0[4]), .out5(decoder_1_out0[5]), .out6(decoder_1_out0[6]), .out7(decoder_1_out0[7]),
    .out8(decoder_1_out0[8]), .out9(decoder_1_out0[9]), .out10(decoder_1_out0[10]),
    .out11(decoder_1_out0[11]), .out12(decoder_1_out0[12]), .out13(decoder_1_out0[13]),
    .out14(decoder_1_out0[14]), .out15(decoder_1_out0[15]), .sel(counter_1_q));  // open: en
  Decoder #(.select(4)) decoder_2 (
    .out0(decoder_2_out0[0]), .out1(decoder_2_out0[1]), .out2(decoder_2_out0[2]), .out3(decoder_2_out0[3]),
    .out4(decoder_2_out0[4]), .out5(decoder_2_out0[5]), .out6(decoder_2_out0[6]), .out7(decoder_2_out0[7]),
    .out8(decoder_2_out0[8]), .out9(decoder_2_out0[9]), .out10(decoder_2_out0[10]),
    .out11(decoder_2_out0[11]), .out12(decoder_2_out0[12]), .out13(decoder_2_out0[13]),
    .out14(decoder_2_out0[14]), .out15(decoder_2_out0[15]), .sel(in_1));  // open: en
  Demultiplexer #(.select(4), .width(16)) demultiplexer_1 (
    .out0(demultiplexer_1_out0), .out1(demultiplexer_1_out1), .out2(demultiplexer_1_out2),
    .out3(demultiplexer_1_out3), .out4(demultiplexer_1_out4), .out5(demultiplexer_1_out5),
    .out6(demultiplexer_1_out6), .out7(demultiplexer_1_out7), .out8(demultiplexer_1_out8),
    .out9(demultiplexer_1_out9), .out10(demultiplexer_1_out10), .out11(demultiplexer_1_out11),
    .out12(demultiplexer_1_out12), .out13(demultiplexer_1_out13), .out14(demultiplexer_1_out14),
    .out15(demultiplexer_1_out15), .in(decoder_1_out0), .sel(counter_2_q));  // open: en
  Demultiplexer #(.select(4), .width(16)) demultiplexer_2 (
    .out0(demultiplexer_1_out0), .out1(demultiplexer_1_out1), .out2(demultiplexer_1_out2),
    .out3(demultiplexer_1_out3), .out4(demultiplexer_1_out4), .out5(demultiplexer_1_out5),
    .out6(demultiplexer_1_out6), .out7(demultiplexer_1_out7), .out8(demultiplexer_1_out8),
    .out9(demultiplexer_1_out9), .out10(demultiplexer_1_out10), .out11(demultiplexer_1_out11),
    .out12(demultiplexer_1_out12), .out13(demultiplexer_1_out13), .out14(demultiplexer_1_out14),
    .out15(demultiplexer_1_out15), .in(decoder_2_out0), .sel(in_2));  // open: en
  DotMatrix #(.inputtype("row"), .matrixcols(16), .matrixrows(16)) dotmatrix_1 (
    .row0(demultiplexer_1_out0), .row1(demultiplexer_1_out1), .row2(demultiplexer_1_out2),
    .row3(demultiplexer_1_out3), .row4(demultiplexer_1_out4), .row5(demultiplexer_1_out5),
    .row6(demultiplexer_1_out6), .row7(demultiplexer_1_out7), .row8(demultiplexer_1_out8),
    .row9(demultiplexer_1_out9), .row10(demultiplexer_1_out10), .row11(demultiplexer_1_out11),
    .row12(demultiplexer_1_out12), .row13(demultiplexer_1_out13), .row14(demultiplexer_1_out14),
    .row15(demultiplexer_1_out15));
  DotMatrix dotmatrix_2 (.col0(in_3), .col1(in_4), .col2(in_5), .col3(in_6), .col4(in_7));
endmodule

module Encoder_8_bits (
  output out_1,
  output out_2,
  output out_3,
  output out_4
);

  wire L_out, N_out, Ne_out, No_out, O_out, S_out, Se_out, So_out;

  Button No (.out(No_out));
  Button O (.out(O_out));
  Button So (.out(So_out));
  Button N (.out(N_out));
  Button Ne (.out(Ne_out));
  Button L (.out(L_out));
  Button Se (.out(Se_out));
  Button S (.out(S_out));
  or or_1 (out_2, No_out, O_out, So_out, S_out);
  or or_2 (out_3, No_out, O_out, Se_out, L_out);
  ExactlyOne xor_1 (
    .out(out_1), .in0(N_out), .in1(Ne_out), .in2(L_out), .in3(Se_out), .in4(S_out), .in5(So_out),
    .in6(O_out), .in7(No_out));
  or or_3 (out_4, No_out, So_out, Se_out, Ne_out);
endmodule

module Multiplexer (
  input  [15:0] in_1,
  input  [15:0] in_2,
  input  [15:0] in_3,
  input  [15:0] in_4,
  input  [15:0] in_5,
  input  [15:0] in_6,
  input  [15:0] in_7,
  input  [15:0] in_8,
  input  [2:0] in_9,
  output [18:0] out_10
);

  wire and_1_out, and_2_out, and_3_out, and_4_out, and_5_out, and_6_out, and_7_out, and_8_out, not_1_out,
       not_2_out, not_3_out, not_4_out, not_5_out, not_6_out, not_7_out, not_8_out, not_9_out, not_10_out,
       not_11_out, not_12_out;

  not not_1 (not_1_out, in_9[2]);
  assign out_10[15:0] = and_2_out ? in_1 : 16'bz;  // Controlled_Buffer controlled_buffer_1
  assign out_10[15:0] = and_1_out ? in_2 : 16'bz;  // Controlled_Buffer controlled_buffer_2
  and and_1 (and_1_out, not_2_out, not_4_out, in_9[0]);
  and and_2 (and_2_out, not_1_out, not_5_out, not_3_out);
  not not_2 (not_2_out, in_9[2]);
  not not_3 (not_3_out, in_9[0]);
  not not_4 (not_4_out, in_9[1]);
  not not_5 (not_5_out, in_9[1]);
  not not_6 (not_6_out, in_9[2]);
  assign out_10[15:0] = and_3_out ? in_3 : 16'bz;  // Controlled_Buffer controlled_buffer_3
  assign out_10[15:0] = and_4_out ? in_4 : 16'bz;  // Controlled_Buffer controlled_buffer_4
  and and_3 (and_3_out, not_6_out, in_9[1], not_8_out);
  and and_4 (and_4_out, not_7_out, in_9[1], in_9[0]);
  not not_7 (not_7_out, in_9[2]);
  not not_8 (not_8_out, in_9[0]);
  assign out_10[15:0] = and_6_out ? in_5 : 16'bz;  // Controlled_Buffer controlled_buffer_5
  assign out_10[15:0] = and_5_out ? in_6 : 16'bz;  // Controlled_Buffer controlled_buffer_6
  and and_5 (and_5_out, in_9[2], not_10_out, in_9[0]);
  and and_6 (and_6_out, in_9[2], not_9_out, not_11_out);
  not not_9 (not_9_out, in_9[1]);
  not not_10 (not_10_out, in_9[1]);
  not not_11 (not_11_out, in_9[0]);
  assign out_10[15:0] = and_8_out ? in_7 : 16'bz;  // Controlled_Buffer controlled_buffer_7
  assign out_10[15:0] = and_7_out ? in_8 : 16'bz;  // Controlled_Buffer controlled_buffer_8
  and and_7 (and_7_out, in_9[2], in_9[1], in_9[0]);
  and and_8 (and_8_out, in_9[2], in_9[1], not_12_out);
  not not_12 (not_12_out, in_9[0]);

  assign out_10[18:16] = in_9;
endmodule

module Demux (
  input  [18:0] in_1,
  output [15:0] out_2,
  output [15:0] out_3,
  output [15:0] out_4,
  output [15:0] out_5,
  output [15:0] out_6,
  output [15:0] out_7,
  output [15:0] out_8,
  output [15:0] out_9
);

  wire and_1_out, and_2_out, and_3_out, and_4_out, and_5_out, and_6_out, and_7_out, and_8_out, not_1_out,
       not_2_out, not_3_out, not_4_out, not_5_out, not_6_out, not_7_out, not_8_out, not_9_out, not_10_out,
       not_11_out, not_12_out;

  assign out_2 = and_2_out ? in_1[15:0] : 16'bz;  // Controlled_Buffer controlled_buffer_1
  assign out_3 = and_1_out ? in_1[15:0] : 16'bz;  // Controlled_Buffer controlled_buffer_2
  and and_1 (and_1_out, not_3_out, not_1_out, in_1[16]);
  and and_2 (and_2_out, not_4_out, not_5_out, not_2_out);
  not not_1 (not_1_out, in_1[17]);
  not not_2 (not_2_out, in_1[16]);
  not not_3 (not_3_out, in_1[18]);
  not not_4 (not_4_out, in_1[18]);
  not not_5 (not_5_out, in_1[17]);
  assign out_4 = and_3_out ? in_1[15:0] : 16'bz;  // Controlled_Buffer controlled_buffer_3
  assign out_5 = and_4_out ? in_1[15:0] : 16'bz;  // Controlled_Buffer controlled_buffer_4
  and and_3 (and_3_out, not_6_out, in_1[17], not_8_out);
  and and_4 (and_4_out, not_7_out, in_1[17], in_1[16]);
  not not_6 (not_6_out, in_1[18]);
  not not_7 (not_7_out, in_1[18]);
  not not_8 (not_8_out, in_1[16]);
  assign out_6 = and_5_out ? in_1[15:0] : 16'bz;  // Controlled_Buffer controlled_buffer_5
  assign out_7 = and_6_out ? in_1[15:0] : 16'bz;  // Controlled_Buffer controlled_buffer_6
  and and_5 (and_5_out, in_1[18], not_10_out, not_11_out);
  and and_6 (and_6_out, in_1[18], not_9_out, in_1[16]);
  not not_9 (not_9_out, in_1[17]);
  not not_10 (not_10_out, in_1[17]);
  not not_11 (not_11_out, in_1[16]);
  assign out_8 = and_8_out ? in_1[15:0] : 16'bz;  // Controlled_Buffer controlled_buffer_7
  assign out_9 = and_7_out ? in_1[15:0] : 16'bz;  // Controlled_Buffer controlled_buffer_8
  and and_7 (and_7_out, in_1[18], in_1[17], in_1[16]);
  and and_8 (and_8_out, in_1[18], in_1[17], not_12_out);
  not not_12 (not_12_out, in_1[16]);
endmodule

module multiplexer_do_logsim (
  input  [7:0] in_1,
  input  [7:0] in_2,
  input  [7:0] in_3,
  input  [7:0] in_4,
  input  [7:0] in_5,
  input  [7:0] in_6,
  input  [7:0] in_7,
  input  [7:0] in_8,
  input  \Subtração ,
  input  Habilitado,
  input  [2:0] in_11,
  input  in_12,
  output [7:0] out_13,
  output [7:0] out_14,
  output [7:0] out_15,
  output [7:0] out_16,
  output [7:0] out_17,
  output [7:0] out_18,
  output [7:0] out_19,
  output [7:0] out_20
);

  wire button_1_out, clock_1_out, clock_2_out, comparator_1_eq, comparator_1_gt, comparator_1_lt,
       counter_1_carry, demultiplexer_2_out0, demultiplexer_2_out1, demultiplexer_2_out2,
       demultiplexer_2_out3, demultiplexer_2_out4, demultiplexer_2_out5, demultiplexer_2_out6,
       demultiplexer_2_out7, or_1_out;
  wire [2:0] counter_1_q, counter_2_q;
  wire [7:0] demultiplexer_1_out0, demultiplexer_1_out1, demultiplexer_1_out2, demultiplexer_1_out3,
       demultiplexer_1_out4, demultiplexer_1_out5, demultiplexer_1_out6, demultiplexer_1_out7,
       multiplexer_1_out;

  Clock clock_1 (.out(clock_1_out));
  Multiplexer_part #(.select(3), .width(8)) multiplexer_1 (
    .in0(in_1), .in1(in_2), .in2(in_3), .in3(in_4), .in4(in_5), .in5(in_6), .in6(in_7), .in7(in_8),
    .out(multiplexer_1_out), .sel(counter_1_q));  // open: en
  Counter #(.width(3), .max('h7)) counter_1 (
    .load(\Subtração ), .count(Habilitado), .Q(counter_1_q), .carry(counter_1_carry), .clk(clock_1_out),
    .clr(or_1_out));  // open: D
  or or_1 (or_1_out, button_1_out, comparator_1_eq);
  Button button_1 (.out(button_1_out));
  Counter #(.width(3), .max('h7)) counter_2 (
    .Q(counter_2_q), .clk(counter_1_carry), .clr(button_1_out));  // open: load, D, count, carry
  Demultiplexer #(.select(3), .width(8)) demultiplexer_1 (
    .out0(demultiplexer_1_out0), .out1(demultiplexer_1_out1), .out2(demultiplexer_1_out2),
    .out3(demultiplexer_1_out3), .out4(demultiplexer_1_out4), .out5(demultiplexer_1_out5),
    .out6(demultiplexer_1_out6), .out7(demultiplexer_1_out7), .in(multiplexer_1_out), .sel(counter_1_q));  // open: en
  Comparator #(.width(3), .mode("unsigned")) comparator_1 (
    .a(counter_2_q), .b(in_11), .gt(comparator_1_gt), .eq(comparator_1_eq), .lt(comparator_1_lt));
  Demultiplexer #(.select(3)) demultiplexer_2 (
    .out0(demultiplexer_2_out0), .out1(demultiplexer_2_out1), .out2(demultiplexer_2_out2),
    .out3(demultiplexer_2_out3), .out4(demultiplexer_2_out4), .out5(demultiplexer_2_out5),
    .out6(demultiplexer_2_out6), .out7(demultiplexer_2_out7), .in(clock_2_out), .sel(counter_1_q));  // open: en
  Clock clock_2 (.out(clock_2_out));
  Register register_1 (
    .D(demultiplexer_1_out0), .en(in_12), .Q(out_13), .clk(demultiplexer_2_out0), .clr(button_1_out));
  Register register_2 (
    .D(demultiplexer_1_out1), .en(in_12), .Q(out_14), .clk(demultiplexer_2_out1), .clr(button_1_out));
  Register register_3 (
    .D(demultiplexer_1_out2), .en(in_12), .Q(out_15), .clk(demultiplexer_2_out2), .clr(button_1_out));
  Register register_4 (
    .D(demultiplexer_1_out3), .en(in_12), .Q(out_16), .clk(demultiplexer_2_out3), .clr(button_1_out));
  Register register_5 (
    .D(demultiplexer_1_out4), .en(in_12), .Q(out_17), .clk(demultiplexer_2_out4), .clr(button_1_out));
  Register register_6 (
    .D(demultiplexer_1_out5), .en(in_12), .Q(out_18), .clk(demultiplexer_2_out5), .clr(button_1_out));
  Register register_7 (
    .D(demultiplexer_1_out6), .en(in_12), .Q(out_19), .clk(demultiplexer_2_out6), .clr(button_1_out));
  Register register_8 (
    .D(demultiplexer_1_out7), .en(in_12), .Q(out_20), .clk(demultiplexer_2_out7), .clr(button_1_out));

  // Notes on the sheet:
  //   Reset
endmodule

module Joystick (
  output [1:0] out_1,
  output [1:0] out_2,
  output [15:0] out_3
);

  wire and_1_out, and_2_out, and_3_out, and_4_out, button_1_out, clock_1_out, clock_2_out,
       controlled_buffer_1_out, controlled_buffer_2_out, controlled_buffer_3_out, controlled_buffer_4_out,
       not_1_out, not_2_out, or_1_out, or_2_out;
  wire [3:0] counter_1_q, counter_2_q;
  wire [15:0] demultiplexer_1_out0, demultiplexer_1_out1, demultiplexer_1_out2, demultiplexer_1_out3,
       demultiplexer_1_out4, demultiplexer_1_out5, demultiplexer_1_out6, demultiplexer_1_out7,
       demultiplexer_1_out8, demultiplexer_1_out9, demultiplexer_1_out10, demultiplexer_1_out11,
       demultiplexer_1_out12, demultiplexer_1_out13, demultiplexer_1_out14, demultiplexer_1_out15;

  Joystick_part #(.bits(2)) joystick_1 (.x(out_1), .y(out_2));
  not not_1 (not_1_out, out_2[1]);
  not not_2 (not_2_out, out_1[1]);
  Clock clock_1 (.out(clock_1_out));
  and and_1 (and_1_out, out_1[0], out_1[1]);
  and and_2 (and_2_out, out_1[0], not_2_out);
  Clock clock_2 (.out(clock_2_out));
  and and_3 (and_3_out, out_2[0], out_2[1]);
  and and_4 (and_4_out, out_2[0], not_1_out);
  assign controlled_buffer_1_out = and_1_out ? clock_1_out : 1'bz;  // Controlled_Buffer controlled_buffer_1
  assign controlled_buffer_2_out = or_1_out ? clock_1_out : 1'bz;  // Controlled_Buffer controlled_buffer_2
  or or_1 (or_1_out, and_1_out, and_2_out);
  assign controlled_buffer_3_out = and_4_out ? clock_2_out : 1'bz;  // Controlled_Buffer controlled_buffer_3
  assign controlled_buffer_4_out = or_2_out ? clock_2_out : 1'bz;  // Controlled_Buffer controlled_buffer_4
  or or_2 (or_2_out, and_3_out, and_4_out);
  Counter #(.width(4), .max('hf), .ongoal("stay")) counter_1 (
    .load(controlled_buffer_1_out), .D(counter_1_q), .count(controlled_buffer_2_out), .Q(counter_1_q),
    .clk(controlled_buffer_2_out), .clr(button_1_out));  // open: carry
  Counter #(.width(4), .max('hf), .ongoal("stay")) counter_2 (
    .load(controlled_buffer_3_out), .D(counter_2_q), .count(controlled_buffer_4_out), .Q(counter_2_q),
    .clk(controlled_buffer_4_out), .clr(button_1_out));  // open: carry
  Button button_1 (.out(button_1_out));
  Decoder #(.select(4)) decoder_1 (
    .out0(out_3[0]), .out1(out_3[1]), .out2(out_3[2]), .out3(out_3[3]), .out4(out_3[4]), .out5(out_3[5]),
    .out6(out_3[6]), .out7(out_3[7]), .out8(out_3[8]), .out9(out_3[9]), .out10(out_3[10]), .out11(out_3[11]),
    .out12(out_3[12]), .out13(out_3[13]), .out14(out_3[14]), .out15(out_3[15]), .sel(counter_1_q));  // open: en
  Demultiplexer #(.select(4), .width(16)) demultiplexer_1 (
    .out0(demultiplexer_1_out0), .out1(demultiplexer_1_out1), .out2(demultiplexer_1_out2),
    .out3(demultiplexer_1_out3), .out4(demultiplexer_1_out4), .out5(demultiplexer_1_out5),
    .out6(demultiplexer_1_out6), .out7(demultiplexer_1_out7), .out8(demultiplexer_1_out8),
    .out9(demultiplexer_1_out9), .out10(demultiplexer_1_out10), .out11(demultiplexer_1_out11),
    .out12(demultiplexer_1_out12), .out13(demultiplexer_1_out13), .out14(demultiplexer_1_out14),
    .out15(demultiplexer_1_out15), .in(out_3), .sel(counter_2_q));  // open: en
  DotMatrix #(.inputtype("row"), .matrixcols(16), .matrixrows(16)) dotmatrix_1 (
    .row0(demultiplexer_1_out0), .row1(demultiplexer_1_out1), .row2(demultiplexer_1_out2),
    .row3(demultiplexer_1_out3), .row4(demultiplexer_1_out4), .row5(demultiplexer_1_out5),
    .row6(demultiplexer_1_out6), .row7(demultiplexer_1_out7), .row8(demultiplexer_1_out8),
    .row9(demultiplexer_1_out9), .row10(demultiplexer_1_out10), .row11(demultiplexer_1_out11),
    .row12(demultiplexer_1_out12), .row13(demultiplexer_1_out13), .row14(demultiplexer_1_out14),
    .row15(demultiplexer_1_out15));
endmodule

module Decodificador (
  input  x,
  input  y,
  input  z,
  output a,
  output b,
  output c,
  output d,
  output e,
  output f,
  output g,
  output h
);

  wire not_1_out, not_2_out, not_3_out, not_4_out, not_5_out, not_6_out, not_7_out, not_8_out, not_9_out,
       not_10_out, not_11_out, not_12_out;

  not not_1 (not_1_out, x);
  not not_2 (not_2_out, y);
  not not_3 (not_3_out, z);
  not not_4 (not_4_out, x);
  not not_5 (not_5_out, y);
  not not_6 (not_6_out, x);
  not not_7 (not_7_out, z);
  not not_8 (not_8_out, x);
  not not_9 (not_9_out, y);
  not not_10 (not_10_out, z);
  not not_11 (not_11_out, y);
  not not_12 (not_12_out, z);
  and and_1 (a, not_1_out, not_2_out, not_3_out);
  and and_2 (b, not_4_out, not_5_out, z);
  and and_3 (c, not_6_out, y, not_7_out);
  and and_4 (d, not_8_out, y, z);
  and and_5 (e, x, not_9_out, not_10_out);
  and and_6 (f, x, not_11_out, z);
  and and_7 (g, x, y, not_12_out);
  and and_8 (h, x, y, z);
endmodule
