// Logisim project Circuitos-M3.circ as structural Verilog: 5 circuits, main circuit main
module main (
  input  _0_Write___1___Load,
  input  Clear,
  output [7:0] out_3
);

  wire clock_1_out, controlled_buffer_1_out, counter_1_carry, not_1_out, not_2_out;
  wire [3:0] counter_1_q;
  wire [7:0] controlled_buffer_2_out, random_1_out;

  Random random_1 (.clk(controlled_buffer_1_out), .out(random_1_out));  // open: next, clr
  Counter #(.width(4), .max('hf)) counter_1 (
    .Q(counter_1_q), .carry(counter_1_carry), .clk(controlled_buffer_1_out));  // open: load, D, count, clr
  not not_1 (not_1_out, counter_1_carry);
  Clock clock_1 (.out(clock_1_out));
  assign controlled_buffer_1_out = not_1_out ? clock_1_out : 1'bz;  // Controlled_Buffer controlled_buffer_1
  assign controlled_buffer_2_out = not_2_out ? random_1_out : 8'bz;  // Controlled_Buffer controlled_buffer_2
  RAM #(.addrWidth(4)) ram_1 (
    .addr(counter_1_q), .data(controlled_buffer_2_out), .clk(controlled_buffer_1_out),
    .ld(_0_Write___1___Load), .clr(Clear));  // open: sel
  not not_2 (not_2_out, _0_Write___1___Load);
  assign out_3 = _0_Write___1___Load ? controlled_buffer_2_out : 8'bz;  // Controlled_Buffer controlled_buffer_3
endmodule

module \Laço_Dependente  (
);

  wire and_1_out, button_1_out, clock_1_out, comparator_1_lt, comparator_2_eq, or_1_out;
  wire [3:0] counter_1_q, counter_2_q;

  Counter #(.width(4), .max('h9)) counter_1 (
    .Q(counter_1_q), .clk(clock_1_out), .clr(and_1_out));  // open: load, D, count, carry
  Clock clock_1 (.out(clock_1_out));
  Button button_1 (.out(button_1_out));
  Comparator #(.width(4), .mode("unsigned")) comparator_1 (
    .a(counter_2_q), .b(counter_1_q), .lt(comparator_1_lt));  // open: gt, eq
  Counter #(.width(4), .max('h9)) counter_2 (
    .Q(counter_2_q), .clk(and_1_out), .clr(or_1_out));  // open: load, D, count, carry
  or or_1 (or_1_out, button_1_out, comparator_2_eq);
  and and_1 (and_1_out, comparator_1_lt, clock_1_out);
  Comparator #(.width(4)) comparator_2 (.a(counter_2_q), .b(4'b0111), .eq(comparator_2_eq));  // open: gt, lt
endmodule

module \Memória  (
  input  in_1,
  input  in_2,
  input  Enable,
  input  in_4,
  output [5:0] out_5
);

  wire and_1_out, clock_1_out, clock_2_out, comparator_1_gt, controlled_buffer_1_out, counter_2_carry,
       counter_3_carry, counter_4_carry, not_1_out, not_2_out;
  wire [3:0] ram_1_data, ram_2_data, selecionador_1__1, selecionador_1__2, selecionador_1__3,
       selecionador_1__4, selecionador_1__5, selecionador_1__6, selecionador_1__7;
  wire [5:0] random_1_out;

  Clock clock_1 (.out(clock_1_out));
  Random #(.width(6), .seed(27)) random_1 (.clk(clock_1_out), .out(random_1_out));  // open: next, clr
  Clock clock_2 (.out(clock_2_out));
  Comparator #(.width(6), .mode("unsigned")) comparator_1 (
    .a(6'b101000), .b(random_1_out), .gt(comparator_1_gt));  // open: eq, lt
  Counter #(.width(6), .max('h27), .ongoal("stay")) counter_1 (
    .Q(out_5), .clk(controlled_buffer_1_out), .clr(in_4));  // open: load, D, count, carry
  assign controlled_buffer_1_out = and_1_out ? clock_2_out : 1'bz;  // Controlled_Buffer controlled_buffer_1
  and and_1 (and_1_out, Enable, not_1_out);
  not not_1 (not_1_out, counter_2_carry);
  RAM #(.addrWidth(6), .dataWidth(4)) ram_1 (
    .addr(random_1_out), .data(ram_1_data), .clk(clock_1_out), .ld(in_1));  // open: sel, clr
  RAM #(.addrWidth(6), .dataWidth(4)) ram_2 (
    .addr(out_5), .data(ram_2_data), .clk(controlled_buffer_1_out), .ld(counter_2_carry), .clr(in_4));  // open: sel
  Selecionador selecionador_1 (
    .in_1(ram_1_data), .Clock(comparator_1_gt), .Clear(in_2), ._4(selecionador_1__4), ._5(selecionador_1__5),
    ._6(selecionador_1__6), ._7(selecionador_1__7), ._1(selecionador_1__1), ._2(selecionador_1__2),
    ._3(selecionador_1__3));
  Counter #(.width(4), .max('ha)) counter_2 (
    .Q(ram_2_data), .carry(counter_2_carry), .clk(counter_4_carry), .clr(in_4));  // open: load, D, count
  Counter #(.width(1), .max('h1), .ongoal("stay")) counter_3 (
    .carry(counter_3_carry), .clk(controlled_buffer_1_out), .clr(in_4));  // open: load, D, count, Q
  Counter #(.width(4), .max('h3)) counter_4 (
    .carry(counter_4_carry), .clk(controlled_buffer_1_out), .clr(not_2_out));  // open: load, D, count, Q
  Register #(.width(4)) register_1 (.D(selecionador_1__5), .clk(comparator_1_gt));  // open: en, Q, clr
  Register #(.width(4)) register_2 (.D(selecionador_1__4), .clk(comparator_1_gt));  // open: en, Q, clr
  Register #(.width(4)) register_3 (.D(selecionador_1__7), .clk(comparator_1_gt));  // open: en, Q, clr
  Register #(.width(4)) register_4 (.D(selecionador_1__1), .clk(comparator_1_gt));  // open: en, Q, clr
  Register #(.width(4)) register_5 (.D(selecionador_1__2), .clk(comparator_1_gt));  // open: en, Q, clr
  not not_2 (not_2_out, counter_3_carry);
  Register #(.width(4)) register_6 (.clk(comparator_1_gt));  // open: D, en, Q, clr
  Register #(.width(4)) register_7 (.D(selecionador_1__3), .clk(comparator_1_gt));  // open: en, Q, clr
endmodule

module Truco (
);

  \Memória  \memória_1  ();  // open: in_1, in_2, Enable, in_4, out_5
endmodule

module Selecionador (
  input  [3:0] in_1,
  input  Clock,
  input  Clear,
  output [3:0] _4,
  output [3:0] _5,
  output [3:0] _6,
  output [3:0] _7,
  output [3:0] _1,
  output [3:0] _2,
  output [3:0] _3
);

  wire and_1_out, and_2_out, and_3_out, and_4_out, and_5_out, and_6_out, and_7_out, controlled_buffer_1_out,
       counter_1_carry, not_1_out, not_2_out, not_3_out, not_4_out, not_5_out, not_6_out, not_7_out,
       not_8_out, not_9_out, not_10_out, not_11_out, not_12_out, not_13_out;
  wire [2:0] counter_1_q;

  assign controlled_buffer_1_out = not_1_out ? Clock : 1'bz;  // Controlled_Buffer controlled_buffer_1
  Counter #(.width(3), .max('h6), .ongoal("stay")) counter_1 (
    .Q(counter_1_q), .carry(counter_1_carry), .clk(controlled_buffer_1_out), .clr(Clear));  // open: load, D, count
  not not_1 (not_1_out, counter_1_carry);
  and and_1 (and_1_out, not_4_out, not_2_out, not_3_out);
  not not_2 (not_2_out, counter_1_q[1]);
  not not_3 (not_3_out, counter_1_q[2]);
  not not_4 (not_4_out, counter_1_q[0]);
  and and_2 (and_2_out, counter_1_q[0], not_5_out, not_6_out);
  not not_5 (not_5_out, counter_1_q[1]);
  not not_6 (not_6_out, counter_1_q[2]);
  assign _4 = and_4_out ? in_1 : 4'bz;  // Controlled_Buffer controlled_buffer_2
  assign _1 = and_1_out ? in_1 : 4'bz;  // Controlled_Buffer controlled_buffer_3
  and and_3 (and_3_out, not_7_out, counter_1_q[1], not_8_out);
  not not_7 (not_7_out, counter_1_q[0]);
  not not_8 (not_8_out, counter_1_q[2]);
  and and_4 (and_4_out, counter_1_q[0], counter_1_q[1], not_11_out);
  and and_5 (and_5_out, not_10_out, not_9_out, counter_1_q[2]);
  not not_9 (not_9_out, counter_1_q[1]);
  not not_10 (not_10_out, counter_1_q[0]);
  not not_11 (not_11_out, counter_1_q[2]);
  assign _5 = and_5_out ? in_1 : 4'bz;  // Controlled_Buffer controlled_buffer_4
  assign _2 = and_2_out ? in_1 : 4'bz;  // Controlled_Buffer controlled_buffer_5
  and and_6 (and_6_out, counter_1_q[0], not_12_out, counter_1_q[2]);
  not not_12 (not_12_out, counter_1_q[1]);
  assign _6 = and_6_out ? in_1 : 4'bz;  // Controlled_Buffer controlled_buffer_6
  assign _3 = and_3_out ? in_1 : 4'bz;  // Controlled_Buffer controlled_buffer_7
  and and_7 (and_7_out, not_13_out, counter_1_q[1], counter_1_q[2]);
  not not_13 (not_13_out, counter_1_q[0]);
  assign _7 = and_7_out ? in_1 : 4'bz;  // Controlled_Buffer controlled_buffer_8
endmodule
